// Logisim project 8bit.circ as structural Verilog: 13 circuits, main circuit main
module main (
  input  in_1,
  input  in_2,
  input  Program_mode,
  output [3:0] out_4
);

  wire A_IN, A_OUT, alu_1_c_out, ALU_OUT, B_IN, button_1_out, button_2_out, clock_1_out, clock_2_out_5,
       COUNTER_ENB, COUNTER_OUT, COUT, decoder_1_out0, decoder_1_out1, decoder_1_out2, decoder_1_out3,
       decoder_1_out4, decoder_1_out5, FLAGS_IN, HALT, INR_IN, INR_OUT, JMP, MAR_IN, multiplexer_3_out,
       not_1_out, not_2_out, or_1_out, OUTPUT_REG_IN, RAM_IN, RAM_OUT, SUB, ZERO, zero_flag_1_out_2;
  wire [3:0] dipswitch_1_sw4, instruct_register_1_out_6, memory_address_reg_1_always_out,
       memory_address_reg_1_data_out, multiplexer_1_out;
  wire [3:3] step_counter_1_out;
  wire [7:0] a_register_1_always_out, alu_1_always_out, b_register_1_out_6, dipswitch_2_sw8,
       multiplexer_2_out, ram_1_always_out;
  wire [7:4] instruct_register_1_out_7;
  wire [10:0] step_counter_1_out_2;

  Button button_1 (.out(button_1_out));
  DipSwitch #(.number(4)) dipswitch_1 (
    .sw1(dipswitch_1_sw4[3]), .sw2(dipswitch_1_sw4[2]), .sw3(dipswitch_1_sw4[1]), .sw4(dipswitch_1_sw4[0]));
  DipSwitch dipswitch_2 (
    .sw1(dipswitch_2_sw8[7]), .sw2(dipswitch_2_sw8[6]), .sw3(dipswitch_2_sw8[5]), .sw4(dipswitch_2_sw8[4]),
    .sw5(dipswitch_2_sw8[3]), .sw6(dipswitch_2_sw8[2]), .sw7(dipswitch_2_sw8[1]), .sw8(dipswitch_2_sw8[0]));
  Clock clock_1 (.out(clock_1_out));
  LED led_1 (.in(not_1_out));
  not not_1 (not_1_out, Program_mode);
  LED led_2 (.in(step_counter_1_out_2[6]));
  buf or_1 (or_1_out, decoder_1_out5);  // OR_Gate
  not not_2 (not_2_out, clock_2_out_5);
  LED led_3 (.in(Program_mode));
  Multiplexer #(.width(4), .enable("false")) multiplexer_1 (
    .in0(memory_address_reg_1_always_out), .in1(dipswitch_1_sw4), .out(multiplexer_1_out), .sel(Program_mode));
  Button button_2 (.out(button_2_out));
  LED led_4 (.in(instruct_register_1_out_6[3]));
  LED led_5 (.in(step_counter_1_out_2[5]));
  LED led_6 (.in(step_counter_1_out_2[3]));
  LED led_7 (.in(step_counter_1_out_2[4]));
  clock clock_2 (.CLK_IN(clock_1_out), .CLK_ENB(in_1), .MANUAL_CLK(in_2), .HALT(HALT), .out_5(clock_2_out_5));
  Multiplexer #(.width(8), .enable("false")) multiplexer_2 (
    .in0({instruct_register_1_out_7, memory_address_reg_1_data_out}), .in1(dipswitch_2_sw8),
    .out(multiplexer_2_out), .sel(Program_mode));
  Multiplexer #(.enable("false")) multiplexer_3 (
    .in0(RAM_IN), .in1(button_2_out), .out(multiplexer_3_out), .sel(Program_mode));
  LED led_8 (.in(ram_1_always_out[7]));
  LED led_9 (.in(instruct_register_1_out_6[2]));
  LED led_10 (.in(instruct_register_1_out_6[1]));
  LED led_11 (.in(instruct_register_1_out_6[0]));
  Step_counter step_counter_1 (
    .Reset(or_1_out), .CLK(not_2_out), .OUT({step_counter_1_out[3], step_counter_1_out_2[2:0]}));
  MEMORY_ADDRESS_REG memory_address_reg_1 (
    .DATA_IN(memory_address_reg_1_data_out), .MAR_IN(MAR_IN), .CLK(clock_2_out_5), .MAR_RESET(button_1_out),
    .ALWAYS_OUT(memory_address_reg_1_always_out), .DATA_OUT(memory_address_reg_1_data_out));  // open: MAR_OUT
  LED led_12 (.in(multiplexer_1_out[3]));
  LED led_13 (.in(multiplexer_1_out[2]));
  LED led_14 (.in(ram_1_always_out[6]));
  LED led_15 (.in(ram_1_always_out[3]));
  LED led_16 (.in(ram_1_always_out[4]));
  LED led_17 (.in(ram_1_always_out[5]));
  INSTRUCT_REGISTER instruct_register_1 (
    .DATA_IN({instruct_register_1_out_7, memory_address_reg_1_data_out}), .STORE(INR_IN),
    .DATA_OUT_ENB(INR_OUT), .RESET(button_1_out), .CLK(clock_2_out_5),
    .out_6({step_counter_1_out_2[6:3], instruct_register_1_out_6}),
    .out_7({instruct_register_1_out_7, memory_address_reg_1_data_out}));
  LED led_18 (.in(multiplexer_1_out[1]));
  LED led_19 (.in(multiplexer_1_out[0]));
  RAM ram_1 (
    .Data(multiplexer_2_out), .Store(multiplexer_3_out), .Clock(clock_2_out_5), .Address(multiplexer_1_out),
    .RAM_OUT_ENB(RAM_OUT), .ALWAYS_OUT(ram_1_always_out),
    .RAM_OUT({instruct_register_1_out_7, memory_address_reg_1_data_out}));
  LED led_20 (.in(ram_1_always_out[0]));
  LED led_21 (.in(ram_1_always_out[1]));
  LED led_22 (.in(ram_1_always_out[2]));
  LED led_23 (.in(decoder_1_out2));
  LED led_24 (.in(decoder_1_out1));
  LED led_25 (.in(decoder_1_out0));
  Decoder #(.select(3)) decoder_1 (
    .out0(decoder_1_out0), .out1(decoder_1_out1), .out2(decoder_1_out2), .out3(decoder_1_out3),
    .out4(decoder_1_out4), .out5(decoder_1_out5), .sel(step_counter_1_out_2[2:0]));  // open: out6, out7, en
  LED led_26 (.in(decoder_1_out4));
  LED led_27 (.in(decoder_1_out3));
  Pull_Resistor pull_resistor_1 (.node(step_counter_1_out_2[10]));
  LED led_28 (.in(instruct_register_1_out_7[7]));
  LED led_29 (.in(instruct_register_1_out_7[6]));
  Pull_Resistor pull_resistor_2 (.node(instruct_register_1_out_7[6]));
  Pull_Resistor pull_resistor_3 (.node(instruct_register_1_out_7[7]));
  LED led_30 (.in(instruct_register_1_out_7[4]));
  LED led_31 (.in(memory_address_reg_1_data_out[2]));
  LED led_32 (.in(memory_address_reg_1_data_out[3]));
  LED led_33 (.in(instruct_register_1_out_7[5]));
  Pull_Resistor pull_resistor_4 (.node(instruct_register_1_out_7[4]));
  Pull_Resistor pull_resistor_5 (.node(memory_address_reg_1_data_out[3]));
  Pull_Resistor pull_resistor_6 (.node(instruct_register_1_out_7[5]));
  Pull_Resistor pull_resistor_7 (.node(memory_address_reg_1_data_out[2]));
  LED led_34 (.in(memory_address_reg_1_data_out[1]));
  LED led_35 (.in(memory_address_reg_1_data_out[0]));
  Pull_Resistor pull_resistor_8 (.node(memory_address_reg_1_data_out[1]));
  Pull_Resistor pull_resistor_9 (.node(memory_address_reg_1_data_out[0]));
  ROM #(.addrWidth(11)) rom_1 (
    .addr({step_counter_1_out_2[10:9], ZERO, COUT, step_counter_1_out_2[6:0]}),
    .data({HALT, MAR_IN, RAM_IN, RAM_OUT, INR_OUT, INR_IN, A_IN, A_OUT}));
  ROM #(.addrWidth(11)) rom_2 (
    .addr({step_counter_1_out_2[10:9], ZERO, COUT, step_counter_1_out_2[6:0]}),
    .data({ALU_OUT, SUB, B_IN, OUTPUT_REG_IN, COUNTER_ENB, COUNTER_OUT, JMP, FLAGS_IN}));
  PC pc_1 (
    .Reset(button_1_out), .Jump(JMP), .count_enable(COUNTER_OUT), .clk(clock_2_out_5),
    .adr_in(memory_address_reg_1_data_out), .counter_out(COUNTER_ENB), .always_out(out_4),
    .adr_out(memory_address_reg_1_data_out));
  OUTPUT_REGISTER output_register_1 (
    .DATA_IN({instruct_register_1_out_7, memory_address_reg_1_data_out}), .STORE(OUTPUT_REG_IN),
    .CLOCK(clock_2_out_5), .RESET(button_1_out));  // open: out_5
  A_register a_register_1 (
    .data_in({instruct_register_1_out_7, memory_address_reg_1_data_out}), .A_in(A_IN), .A_out(A_OUT),
    .clk(clock_2_out_5), .A_reset(button_1_out), .always_out(a_register_1_always_out),
    .data_out({instruct_register_1_out_7, memory_address_reg_1_data_out}));
  ALU alu_1 (
    .A_IN(a_register_1_always_out), .B_IN(b_register_1_out_6), .Output_ENB(ALU_OUT), .SUB(SUB),
    .Always_Out(alu_1_always_out), .ALU_Data_Out({instruct_register_1_out_7, memory_address_reg_1_data_out}),
    .C_OUT(alu_1_c_out));
  B_register b_register_1 (
    .in_1({instruct_register_1_out_7, memory_address_reg_1_data_out}), .B_IN(B_IN), .CLK(clock_2_out_5),
    .B_RESET(button_1_out), .out_6(b_register_1_out_6),
    .out_7({instruct_register_1_out_7, memory_address_reg_1_data_out}));  // open: B_OUT
  Zero_Flag zero_flag_1 (.in_1(alu_1_always_out), .out_2(zero_flag_1_out_2));
  LED led_36 (.in(RAM_IN));
  LED led_37 (.in(MAR_IN));
  LED led_38 (.in(RAM_OUT));
  LED led_39 (.in(HALT));
  LED led_40 (.in(A_IN));
  LED led_41 (.in(INR_OUT));
  LED led_42 (.in(INR_IN));
  LED led_43 (.in(A_OUT));
  LED led_44 (.in(SUB));
  LED led_45 (.in(B_IN));
  LED led_46 (.in(ALU_OUT));
  LED led_47 (.in(OUTPUT_REG_IN));
  FLAGS flags_1 (
    .Carry(alu_1_c_out), .Zero(zero_flag_1_out_2), .Store(FLAGS_IN), .Clk(clock_2_out_5),
    .Reset(button_1_out), .CARRY_OUT(COUT), .ZERO_OUT(ZERO));
  LED led_48 (.in(FLAGS_IN));
  LED led_49 (.in(COUNTER_OUT));
  LED led_50 (.in(COUNTER_ENB));
  LED led_51 (.in(JMP));
endmodule

module clock (
  input  CLK_IN,
  input  CLK_ENB,
  input  MANUAL_CLK,
  input  HALT,
  output out_5
);

  wire and_1_out, and_2_out, not_1_out, not_2_out, or_1_out;

  not not_1 (not_1_out, CLK_ENB);
  not not_2 (not_2_out, HALT);
  and and_1 (and_1_out, CLK_IN, CLK_ENB);
  and and_2 (and_2_out, not_1_out, MANUAL_CLK);
  or or_1 (or_1_out, and_1_out, and_2_out);
  and and_3 (out_5, or_1_out, not_2_out);
endmodule

module PC (
  input  Reset,
  input  Jump,
  input  count_enable,
  input  clk,
  input  [3:0] adr_in,
  input  counter_out,
  output [3:0] always_out,
  output [3:0] adr_out
);

  Counter #(.width(4), .max('hf)) counter_1 (
    .clr(Reset), .load(Jump), .up(count_enable), .count(count_enable), .clk(clk), .D(adr_in), .Q(always_out));  // open: carry
  assign adr_out = counter_out ? always_out : 4'bz;  // Controlled_Buffer controlled_buffer_1
endmodule

module A_register (
  input  [7:0] data_in,
  input  A_in,
  input  A_out,
  input  clk,
  input  A_reset,
  output [7:0] always_out,
  output [7:0] data_out
);

  Register register_1 (.D(data_in), .en(A_in), .clk(clk), .Q(always_out), .clr(A_reset));
  assign data_out = A_out ? always_out : 8'bz;  // Controlled_Buffer controlled_buffer_1
endmodule

module ALU (
  input  [7:0] A_IN,
  input  [7:0] B_IN,
  input  Output_ENB,
  input  SUB,
  output [7:0] Always_Out,
  output [7:0] ALU_Data_Out,
  output C_OUT
);

  wire not_1_out;
  wire [7:0] controlled_buffer_1_out, xor_1_out;

  assign controlled_buffer_1_out = SUB ? {8{1'b1}} : 8'bz;  // Controlled_Buffer controlled_buffer_1
  not not_1 (not_1_out, SUB);
  assign controlled_buffer_1_out = not_1_out ? {8{1'b0}} : 8'bz;  // Controlled_Buffer controlled_buffer_2
  assign xor_1_out = B_IN ^ controlled_buffer_1_out;  // XOR_Gate xor_1, 8 bits wide
  Adder adder_1 (.a(A_IN), .b(xor_1_out), .out(Always_Out), .cin(SUB), .cout(C_OUT));
  assign ALU_Data_Out = Output_ENB ? Always_Out : 8'bz;  // Controlled_Buffer controlled_buffer_3
endmodule

module B_register (
  input  [7:0] in_1,
  input  B_IN,
  input  B_OUT,
  input  CLK,
  input  B_RESET,
  output [7:0] out_6,
  output [7:0] out_7
);

  Register register_1 (.D(in_1), .en(B_IN), .clk(CLK), .Q(out_6), .clr(B_RESET));
  assign out_7 = B_OUT ? out_6 : 8'bz;  // Controlled_Buffer controlled_buffer_1
endmodule

module OUTPUT_REGISTER (
  input  [7:0] DATA_IN,
  input  STORE,
  input  CLOCK,
  input  RESET,
  output [7:0] out_5
);

  Register register_1 (.D(DATA_IN), .en(STORE), .clk(CLOCK), .Q(out_5), .clr(RESET));
endmodule

module MEMORY_ADDRESS_REG (
  input  [3:0] DATA_IN,
  input  MAR_IN,
  input  MAR_OUT,
  input  CLK,
  input  MAR_RESET,
  output [3:0] ALWAYS_OUT,
  output [3:0] DATA_OUT
);

  Register #(.width(4)) register_1 (.D(DATA_IN), .en(MAR_IN), .clk(CLK), .Q(ALWAYS_OUT), .clr(MAR_RESET));
  assign DATA_OUT = MAR_OUT ? ALWAYS_OUT : 4'bz;  // Controlled_Buffer controlled_buffer_1
endmodule

module RAM (
  input  [7:0] Data,
  input  Store,
  input  Clock,
  input  [3:0] Address,
  input  RAM_OUT_ENB,
  output [7:0] ALWAYS_OUT,
  output [7:0] RAM_OUT
);

  wire and_1_out, and_2_out, and_3_out, and_4_out, and_5_out, and_6_out, and_7_out, and_8_out, and_9_out,
       and_10_out, and_11_out, and_12_out, and_13_out, and_14_out, and_15_out, and_16_out, decoder_1_out0,
       decoder_1_out1, decoder_1_out2, decoder_1_out3, decoder_1_out4, decoder_1_out5, decoder_1_out6,
       decoder_1_out7, decoder_1_out8, decoder_1_out9, decoder_1_out10, decoder_1_out11, decoder_1_out12,
       decoder_1_out13, decoder_1_out14, decoder_1_out15;
  wire [7:0] demultiplexer_1_out0, demultiplexer_1_out1, demultiplexer_1_out2, demultiplexer_1_out3,
       demultiplexer_1_out4, demultiplexer_1_out5, demultiplexer_1_out6, demultiplexer_1_out7,
       demultiplexer_1_out8, demultiplexer_1_out9, demultiplexer_1_out10, demultiplexer_1_out11,
       demultiplexer_1_out12, demultiplexer_1_out13, demultiplexer_1_out14, demultiplexer_1_out15,
       register_1_q, register_2_q, register_3_q, register_4_q, register_5_q, register_6_q, register_7_q,
       register_8_q, register_9_q, register_10_q, register_11_q, register_12_q, register_13_q, register_14_q,
       register_15_q, register_16_q;

  Demultiplexer #(.select(4), .width(8), .enable("false")) demultiplexer_1 (
    .out0(demultiplexer_1_out0), .out1(demultiplexer_1_out1), .out2(demultiplexer_1_out2),
    .out3(demultiplexer_1_out3), .out4(demultiplexer_1_out4), .out5(demultiplexer_1_out5),
    .out6(demultiplexer_1_out6), .out7(demultiplexer_1_out7), .out8(demultiplexer_1_out8),
    .out9(demultiplexer_1_out9), .out10(demultiplexer_1_out10), .out11(demultiplexer_1_out11),
    .out12(demultiplexer_1_out12), .out13(demultiplexer_1_out13), .out14(demultiplexer_1_out14),
    .out15(demultiplexer_1_out15), .in(Data), .sel(Address));
  Decoder #(.select(4)) decoder_1 (
    .out0(decoder_1_out0), .out1(decoder_1_out1), .out2(decoder_1_out2), .out3(decoder_1_out3),
    .out4(decoder_1_out4), .out5(decoder_1_out5), .out6(decoder_1_out6), .out7(decoder_1_out7),
    .out8(decoder_1_out8), .out9(decoder_1_out9), .out10(decoder_1_out10), .out11(decoder_1_out11),
    .out12(decoder_1_out12), .out13(decoder_1_out13), .out14(decoder_1_out14), .out15(decoder_1_out15),
    .sel(Address));  // open: en
  and and_1 (and_1_out, decoder_1_out0, Store);
  and and_2 (and_2_out, decoder_1_out1, Store);
  and and_3 (and_3_out, decoder_1_out2, Store);
  and and_4 (and_4_out, decoder_1_out3, Store);
  and and_5 (and_5_out, decoder_1_out4, Store);
  and and_6 (and_6_out, decoder_1_out5, Store);
  and and_7 (and_7_out, decoder_1_out6, Store);
  and and_8 (and_8_out, decoder_1_out7, Store);
  and and_9 (and_9_out, decoder_1_out8, Store);
  and and_10 (and_10_out, decoder_1_out9, Store);
  and and_11 (and_11_out, decoder_1_out10, Store);
  and and_12 (and_12_out, decoder_1_out11, Store);
  and and_13 (and_13_out, decoder_1_out12, Store);
  and and_14 (and_14_out, decoder_1_out13, Store);
  and and_15 (and_15_out, decoder_1_out14, Store);
  and and_16 (and_16_out, decoder_1_out15, Store);
  Register register_1 (.D(demultiplexer_1_out0), .en(and_1_out), .clk(Clock), .Q(register_1_q));  // open: clr
  Register register_2 (.D(demultiplexer_1_out1), .en(and_2_out), .clk(Clock), .Q(register_2_q));  // open: clr
  Register register_3 (.D(demultiplexer_1_out2), .en(and_3_out), .clk(Clock), .Q(register_3_q));  // open: clr
  Register register_4 (.D(demultiplexer_1_out3), .en(and_4_out), .clk(Clock), .Q(register_4_q));  // open: clr
  Register register_5 (.D(demultiplexer_1_out4), .en(and_5_out), .clk(Clock), .Q(register_5_q));  // open: clr
  Register register_6 (.D(demultiplexer_1_out5), .en(and_6_out), .clk(Clock), .Q(register_6_q));  // open: clr
  Register register_7 (.D(demultiplexer_1_out6), .en(and_7_out), .clk(Clock), .Q(register_7_q));  // open: clr
  Register register_8 (.D(demultiplexer_1_out7), .en(and_8_out), .clk(Clock), .Q(register_8_q));  // open: clr
  Register register_9 (.D(demultiplexer_1_out8), .en(and_9_out), .clk(Clock), .Q(register_9_q));  // open: clr
  Register register_10 (.D(demultiplexer_1_out9), .en(and_10_out), .clk(Clock), .Q(register_10_q));  // open: clr
  Register register_11 (.D(demultiplexer_1_out10), .en(and_11_out), .clk(Clock), .Q(register_11_q));  // open: clr
  Register register_12 (.D(demultiplexer_1_out11), .en(and_12_out), .clk(Clock), .Q(register_12_q));  // open: clr
  Register register_13 (.D(demultiplexer_1_out12), .en(and_13_out), .clk(Clock), .Q(register_13_q));  // open: clr
  Register register_14 (.D(demultiplexer_1_out13), .en(and_14_out), .clk(Clock), .Q(register_14_q));  // open: clr
  Register register_15 (.D(demultiplexer_1_out14), .en(and_15_out), .clk(Clock), .Q(register_15_q));  // open: clr
  Register register_16 (.D(demultiplexer_1_out15), .en(and_16_out), .clk(Clock), .Q(register_16_q));  // open: clr
  Multiplexer #(.select(4), .width(8), .enable("false")) multiplexer_1 (
    .in0(register_1_q), .in1(register_2_q), .in2(register_3_q), .in3(register_4_q), .in4(register_5_q),
    .in5(register_6_q), .in6(register_7_q), .in7(register_8_q), .in8(register_9_q), .in9(register_10_q),
    .in10(register_11_q), .in11(register_12_q), .in12(register_13_q), .in13(register_14_q),
    .in14(register_15_q), .in15(register_16_q), .out(ALWAYS_OUT), .sel(Address));
  assign RAM_OUT = RAM_OUT_ENB ? ALWAYS_OUT : 8'bz;  // Controlled_Buffer controlled_buffer_1
endmodule

module INSTRUCT_REGISTER (
  input  [7:0] DATA_IN,
  input  STORE,
  input  DATA_OUT_ENB,
  input  RESET,
  input  CLK,
  output [7:0] out_6,
  output [7:0] out_7
);

  wire [7:4] pull_resistor_1_node;

  Register register_1 (.D(DATA_IN), .en(STORE), .clk(CLK), .Q(out_6), .clr(RESET));
  Pull_Resistor pull_resistor_1 (.node(pull_resistor_1_node[4]));
  Pull_Resistor pull_resistor_2 (.node(pull_resistor_1_node[5]));
  Pull_Resistor pull_resistor_3 (.node(pull_resistor_1_node[6]));
  Pull_Resistor pull_resistor_4 (.node(pull_resistor_1_node[7]));
  assign out_7 = DATA_OUT_ENB ? {pull_resistor_1_node, out_6[3:0]} : 8'bz;  // Controlled_Buffer controlled_buffer_1
endmodule

module Step_counter (
  input  Reset,
  input  CLK,
  output [3:0] OUT
);

  Counter #(.width(4), .max('hf)) counter_1 (
    .clr(Reset), .up(1'b1), .count(1'b1), .clk(CLK), .Q(OUT));  // open: load, D, carry
endmodule

module Zero_Flag (
  input  [7:0] in_1,
  output out_2
);

  wire and_1_out, and_2_out, nor_1_out, nor_2_out, nor_3_out, nor_4_out;

  nor nor_1 (nor_1_out, in_1[0], in_1[1]);
  nor nor_2 (nor_2_out, in_1[2], in_1[3]);
  nor nor_3 (nor_3_out, in_1[4], in_1[5]);
  nor nor_4 (nor_4_out, in_1[6], in_1[7]);
  and and_1 (and_1_out, nor_1_out, nor_2_out);
  and and_2 (and_2_out, nor_3_out, nor_4_out);
  and and_3 (out_2, and_1_out, and_2_out);
endmodule

module FLAGS (
  input  Carry,
  input  Zero,
  input  Store,
  input  Clk,
  input  Reset,
  output CARRY_OUT,
  output ZERO_OUT
);

  Register #(.width(1)) register_1 (.D(Carry), .en(Store), .clk(Clk), .Q(CARRY_OUT), .clr(Reset));
  Register #(.width(1)) register_2 (.D(Zero), .en(Store), .clk(Clk), .Q(ZERO_OUT), .clr(Reset));
endmodule
